# Fritzing sketch final_fritzing (saved by Fritzing 1.0.3b)
breadboards: 2

parts:
  U1 = ESP32-38PinWide [part_number=ESP32-38PinWide]
  FC-1 = Sound Sensor
  Parça1 = RFID-RC522-v2
  R1 = Resistor [tolerance=±5% resistance=220 package="2512 [SMD]"]
  R2 = Resistor [tolerance=±5% resistance=220 package="2512 [SMD]"]
  R3 = Resistor [tolerance=±5% resistance=220 package="2512 [SMD]"]
  LED1 = RGB LED (com. cathode, rbg) [color="Red (633nm)" current=0.030A package="5 mm [THT]"]
  J1 = Basic Servo

nets:
  VCC: U1.3.3, FC-1.VCC, Parça1.3.3V
  N1: U1.GPIO32, FC-1.OUT
  N2: U1.GPIO33, R1.Pin_1
  N3: U1.GPIO25, R3.Pin_0
  N4: U1.GPIO26, R2.Pin_1
  N5: U1.GPIO27, J1.pulse
  GND: U1.GPIO11, FC-1.GND, Parça1.GND, J1.gnd
  VIN: U1.VIN, J1.vcc
  N6: U1.GPIO18, Parça1.SCK
  N7: U1.GPIO19, Parça1.MISO
  N8: U1.GPIO21, Parça1.SDA
  N9: U1.GPIO22, Parça1.RST
  N10: U1.GPIO23, Parça1.MOSI
  N11: R1.Pin_0, LED1.green_anode
  N12: R2.Pin_0, LED1.red_anode
  N13: R3.Pin_1, LED1.blue_anode

custom parts:
  ESP32-38PinWide: Generic 38-Pin ESP32 with wide format (only access to one side of pins on a breadboard) based on Stephen Lilley's HiLetgo ESP-WROOM-32 ESP32 ESP-32S Development Board.
  RFID-RC522-v2: A simple China made RFID-RC522 Reader; do check the pin labels, as this is a MFRC522 based clone.
